// Logisim project ALU8.circ as structural Verilog: 2 circuits, main circuit main
module main (
  input  [7:0] A,
  input  [7:0] B,
  input  Cin,
  input  [3:0] Op,
  output Cout,
  output ZF,
  output SF,
  output OF,
  output [7:0] F
);

  ALU alu_1 (.A(A), .B(B), .Cin(Cin), .Cout(Cout), .ZF(ZF), .SF(SF), .OF(OF), .Op(Op), .F(F));
endmodule

module ALU (
  input  [7:0] A,
  input  [7:0] B,
  input  Cin,
  input  [3:0] Op,
  output Cout,
  output ZF,
  output SF,
  output OF,
  output [7:0] F
);
endmodule
